# Fritzing sketch wiring (saved by Fritzing 0.9.5d)

parts:
  Mod1 = Raspberry Pi 4B
  HC-SR04_Sensor_2 = HC-SR04 Ultrasonic Distance Sensor
  HC-SR04_Sensor_3 = Fan
  Fan1 = Touch screen  # not connected

nets:
  3V3: Mod1.3V3, HC-SR04_Sensor_2.VCC
  5V: Mod1.5V, HC-SR04_Sensor_3.VCC
  GND: Mod1.GND, HC-SR04_Sensor_2.GND, HC-SR04_Sensor_3.GND
  N1: Mod1.GPIO4, HC-SR04_Sensor_2.TRIG
  N2: Mod1.GPIO14, HC-SR04_Sensor_3.IN
  N3: Mod1.GPIO17, HC-SR04_Sensor_2.ECHO

custom parts:
  HC-SR04 Ultrasonic Distance Sensor: The HC-SR04 is an ultrasonic distance sensor. It is capable of providing measurement for ranges of 2cm to 400cm. The module operates at 5V.
